// Logisim project Going Overboard Again.circ as structural Verilog: 1 circuit, main circuit main
module main (
);

  wire _0_2_out, _0_Check_out, _0_out, _0ERR_out, _1_2_out, _1_out, _2_2_out, _2_out, _3_2_out, _3_out,
       _4_2_out, _4_out, _5_2_out, _5_out, _6_2_out, _6_out, _7_2_out, _7_out, _8_2_out, _8_out, _9_2_out,
       _9_out, Check_out, d_ff_1_q, d_ff_2_q, d_ff_3_q, d_ff_5_q, d_ff_6_q, d_ff_7_q, d_ff_9_q, d_ff_9_qn,
       d_ff_10_qn, decoder_3_out0, decoder_3_out1, decoder_3_out2, decoder_3_out3, decoder_3_out4,
       decoder_3_out5, decoder_3_out6, decoder_3_out7, decoder_3_out8, decoder_3_out9, decoder_3_out10,
       decoder_3_out11, decoder_3_out12, decoder_3_out13, decoder_3_out14, decoder_4_out0, decoder_4_out1,
       decoder_4_out2, decoder_4_out3, decoder_4_out4, decoder_4_out5, decoder_4_out6, decoder_4_out7,
       decoder_4_out8, decoder_4_out9, decoder_4_out10, decoder_4_out11, decoder_4_out12, decoder_4_out13,
       decoder_4_out14, decoder_4_out15, decoder_7_out0, decoder_7_out1, decoder_7_out2, decoder_7_out3,
       decoder_7_out4, decoder_7_out5, decoder_7_out6, decoder_7_out7, decoder_7_out8, decoder_7_out9,
       decoder_7_out10, decoder_7_out11, decoder_7_out12, decoder_7_out13, decoder_7_out14, decoder_7_out15,
       Hundreds_2_out, Hundreds_out, P_0XX_out, subtractor_1_bout, transistor_4_out, transistor_5_out,
       transistor_6_out, transistor_12_out, transistor_13_out, X_0XX_3_out, X_0XX_4_out, X_0XX_out,
       X_1XX_2_out, X_1XX_4_out, X_1XX_5_out, X_1XX_out, X_X0X_2_out, X_X0X_4_out, X_X0X_5_out, X_X0X_6_out,
       X_X1X_2_out, X_X1X_4_out, X_X1X_5_out, X_X1X_6_out, X_X2X_3_out, X_X2X_4_out, X_X2X_5_out,
       X_X2X_8_out, X_X3X_3_out, X_X3X_5_out, X_X3X_6_out, X_X3X_7_out, X_X3X_out, X_X4X_2_out, X_X4X_4_out,
       X_X5X_2_out, X_X5X_4_out, X_X6X_2_out, X_X6X_3_out, X_X6X_4_out, X_X7X_2_out, X_X7X_3_out,
       X_X8X_2_out, X_X8X_3_out, X_X9X_2_out, X_X9X_3_out, X_X9X_6_out, X_X9X_out;
  wire [1:0] _2_0X_2_out, _2_0X_out;
  wire [2:0] _2_3_out, BR_3_out, BR_5_out, BR_6_out, BR_7_out, BR_out, TR_3_out, X_0XX_2_out, X_X0X_3_out;
  wire [3:0] adder_1_out, and_3_out, d_ff_1_qn, d_ff_5_qn, divider_1_out, multiplier_1_cout,
       multiplier_1_out, subtractor_1_out, TR_5_out, TR_6_out, TR_7_out, TR_out, transistor_1_out,
       transistor_2_out, X_X0X_out;
  wire [4:0] Sign_out_2, Sign_out_3, Sign_out_4, undriven_7, undriven_8, undriven_9, X_XX0_2_out, X_XX0_out,
       X_XX5_out;
  wire [4:4] adder_1_cout;
  wire [5:0] BR_2_out, X_X4X_out;
  wire [6:0] BR_4_out;
  wire [7:0] transistor_3_out, X_X2X_2_out;
  wire [9:0] decoder_22_out6, Mult_Ones_out, Ones_out, P_X0X_out, P_XX0_out, Sign_out, Tens_2_out,
       Tens_3_out, Tens_out, undriven_6, X_X0X_7_out, X_XX0_3_out, X_XX0_4_out, X_XX0_5_out, X_XX0_6_out,
       X_XX0_7_out;
  wire [9:5] X_XX5_2_out;
  wire [14:0] undriven;
  wire [15:0] decoder_2_out0, decoder_5_out0, decoder_6_out0, decoder_8_out0, decoder_9_out0,
       decoder_10_out0, decoder_11_out0, decoder_12_out0, decoder_13_out0, decoder_14_out0, decoder_15_out0,
       decoder_16_out0, decoder_17_out0, decoder_20_out0, decoder_21_out0, decoder_22_out0, MN_2_out, MN_out;
  wire [23:1] undriven_3;
  wire [24:0] transistor_7_out, transistor_8_out, transistor_10_out, transistor_11_out, undriven_2,
       undriven_4, undriven_5;
  wire [29:0] PM_out;
  wire [30:0] decoder_1_out0, transistor_9_out;
  wire [31:0] decoder_18_out0;

  Decoder #(.select(5)) decoder_1 (
    .out0(decoder_1_out0[0]), .out1(decoder_1_out0[1]), .out2(decoder_1_out0[2]), .out3(decoder_1_out0[3]),
    .out4(decoder_1_out0[4]), .out5(decoder_1_out0[5]), .out6(decoder_1_out0[6]), .out7(decoder_1_out0[7]),
    .out8(decoder_1_out0[8]), .out9(decoder_1_out0[9]), .out10(decoder_1_out0[10]),
    .out11(decoder_1_out0[11]), .out12(decoder_1_out0[12]), .out13(decoder_1_out0[13]),
    .out14(decoder_1_out0[14]), .out15(decoder_1_out0[15]), .out16(decoder_1_out0[16]),
    .out17(decoder_1_out0[17]), .out18(decoder_1_out0[18]), .out19(decoder_1_out0[19]),
    .out20(decoder_1_out0[20]), .out21(decoder_1_out0[21]), .out22(decoder_1_out0[22]),
    .out23(decoder_1_out0[23]), .out24(decoder_1_out0[24]), .out25(decoder_1_out0[25]),
    .out26(decoder_1_out0[26]), .out27(decoder_1_out0[27]), .out28(decoder_1_out0[28]),
    .out29(decoder_1_out0[29]), .out30(decoder_1_out0[30]), .sel({adder_1_cout[4], adder_1_out}),
    .en(and_3_out[3]));  // open: out31
  Decoder #(.select(4)) decoder_2 (
    .out0(decoder_2_out0[0]), .out1(decoder_2_out0[1]), .out2(decoder_2_out0[2]), .out3(decoder_2_out0[3]),
    .out4(decoder_2_out0[4]), .out5(decoder_2_out0[5]), .out6(decoder_2_out0[6]), .out7(decoder_2_out0[7]),
    .out8(decoder_2_out0[8]), .out9(decoder_2_out0[9]), .out10(decoder_2_out0[10]),
    .out11(decoder_2_out0[11]), .out12(decoder_2_out0[12]), .out13(decoder_2_out0[13]),
    .out14(decoder_2_out0[14]), .out15(decoder_2_out0[15]), .sel(transistor_1_out), .en(and_3_out[2]));
  Decoder #(.select(4)) decoder_3 (
    .out0(decoder_3_out0), .out1(decoder_3_out1), .out2(decoder_3_out2), .out3(decoder_3_out3),
    .out4(decoder_3_out4), .out5(decoder_3_out5), .out6(decoder_3_out6), .out7(decoder_3_out7),
    .out8(decoder_3_out8), .out9(decoder_3_out9), .out10(decoder_3_out10), .out11(decoder_3_out11),
    .out12(decoder_3_out12), .out13(decoder_3_out13), .out14(decoder_3_out14), .sel(multiplier_1_cout),
    .en(and_3_out[1]));  // open: out15
  D_Flip_Flop d_ff_1 (.clk(_2_3_out[2]), .D(d_ff_1_qn[0]), .Q(d_ff_1_q), .Qn(d_ff_1_qn[0]));  // open: preset, en, reset
  D_Flip_Flop d_ff_2 (.clk(d_ff_1_q), .D(d_ff_1_qn[1]), .Q(d_ff_2_q), .Qn(d_ff_1_qn[1]));  // open: preset, en, reset
  or _2_0X (_2_0X_out[0], decoder_4_out0, decoder_4_out1, decoder_4_out2, decoder_4_out3, decoder_4_out4, decoder_4_out5, decoder_4_out6, decoder_4_out7, decoder_4_out8, decoder_4_out9);
  Transistor #(.width(4)) transistor_1 (.in(subtractor_1_out), .out(transistor_1_out), .gate(subtractor_1_bout));
  D_Flip_Flop d_ff_3 (.clk(d_ff_2_q), .D(d_ff_1_qn[2]), .Q(d_ff_3_q), .Qn(d_ff_1_qn[2]));  // open: preset, en, reset
  Decoder #(.select(4)) decoder_4 (
    .out0(decoder_4_out0), .out1(decoder_4_out1), .out2(decoder_4_out2), .out3(decoder_4_out3),
    .out4(decoder_4_out4), .out5(decoder_4_out5), .out6(decoder_4_out6), .out7(decoder_4_out7),
    .out8(decoder_4_out8), .out9(decoder_4_out9), .out10(decoder_4_out10), .out11(decoder_4_out11),
    .out12(decoder_4_out12), .out13(decoder_4_out13), .out14(decoder_4_out14), .out15(decoder_4_out15),
    .sel(d_ff_1_qn), .en(1'b1));
  Adder #(.width(4)) adder_1 (.a(d_ff_1_qn), .b(d_ff_5_qn), .out(adder_1_out), .cout(adder_1_cout[4]));  // open: cin
  Subtractor #(.width(4)) subtractor_1 (
    .a(d_ff_1_qn), .b(d_ff_5_qn), .out(subtractor_1_out), .bout(subtractor_1_bout));  // open: bin
  Transistor #(.\type ("n"), .gate("br"), .width(4)) transistor_2 (
    .in(subtractor_1_out), .out(transistor_2_out), .gate(subtractor_1_bout));
  Decoder #(.select(4)) decoder_5 (
    .out0(decoder_5_out0[15]), .out1(decoder_5_out0[14]), .out2(decoder_5_out0[13]),
    .out3(decoder_5_out0[12]), .out4(decoder_5_out0[11]), .out5(decoder_5_out0[10]),
    .out6(decoder_5_out0[9]), .out7(decoder_5_out0[8]), .out8(decoder_5_out0[7]), .out9(decoder_5_out0[6]),
    .out10(decoder_5_out0[5]), .out11(decoder_5_out0[4]), .out12(decoder_5_out0[3]),
    .out13(decoder_5_out0[2]), .out14(decoder_5_out0[1]), .out15(decoder_5_out0[0]), .sel(transistor_2_out),
    .en(and_3_out[2]));
  D_Flip_Flop d_ff_4 (.clk(d_ff_3_q), .D(d_ff_1_qn[3]), .Qn(d_ff_1_qn[3]));  // open: Q, preset, en, reset
  assign MN_out = decoder_2_out0 | decoder_6_out0;  // OR_Gate MN, 16 bits wide
  Decoder #(.select(4)) decoder_6 (
    .out0(decoder_6_out0[0]), .out1(decoder_6_out0[1]), .out2(decoder_6_out0[2]), .out3(decoder_6_out0[3]),
    .out4(decoder_6_out0[4]), .out5(decoder_6_out0[5]), .out6(decoder_6_out0[6]), .out7(decoder_6_out0[7]),
    .out8(decoder_6_out0[8]), .out9(decoder_6_out0[9]), .out10(decoder_6_out0[10]),
    .out11(decoder_6_out0[11]), .out12(decoder_6_out0[12]), .out13(decoder_6_out0[13]),
    .out14(decoder_6_out0[14]), .out15(decoder_6_out0[15]), .sel(divider_1_out), .en(and_3_out[0]));
  Transistor #(.\type ("n"), .width(8)) transistor_3 (
    .in({d_ff_5_qn, d_ff_1_qn}), .out(transistor_3_out), .gate(and_3_out[1]));
  D_Flip_Flop d_ff_5 (.clk(_2_3_out[0]), .D(d_ff_5_qn[0]), .Q(d_ff_5_q), .Qn(d_ff_5_qn[0]));  // open: preset, en, reset
  or _2_1X (_2_0X_out[1], decoder_4_out10, decoder_4_out11, decoder_4_out12, decoder_4_out13, decoder_4_out14, decoder_4_out15);
  or _0 (_0_out, decoder_4_out0, decoder_4_out10);
  or _1 (_1_out, decoder_4_out1, decoder_4_out11);
  or _2 (_2_out, decoder_4_out2, decoder_4_out12);
  or _3 (_3_out, decoder_4_out3, decoder_4_out13);
  or _4 (_4_out, decoder_4_out4, decoder_4_out14);
  or _5 (_5_out, decoder_4_out5, decoder_4_out15);
  buf _6 (_6_out, decoder_4_out6);
  buf _7 (_7_out, decoder_4_out7);
  buf _8 (_8_out, decoder_4_out8);
  buf _9 (_9_out, decoder_4_out9);
  assign MN_2_out = {decoder_5_out0[14:0], decoder_5_out0[15]} | MN_out;  // OR_Gate MN_2, 16 bits wide
  Divider #(.width(4)) divider_1 (.a(d_ff_1_qn), .b(d_ff_5_qn), .out(divider_1_out));  // open: upper, rem
  Multiplier #(.width(4)) multiplier_1 (
    .a(transistor_3_out[3:0]), .b(transistor_3_out[7:4]), .out(multiplier_1_out), .cout(multiplier_1_cout));  // open: cin
  D_Flip_Flop d_ff_6 (.clk(d_ff_5_q), .D(d_ff_5_qn[1]), .Q(d_ff_6_q), .Qn(d_ff_5_qn[1]));  // open: preset, en, reset
  or _2_0X_2 (_2_0X_2_out[0], decoder_7_out0, decoder_7_out1, decoder_7_out2, decoder_7_out3, decoder_7_out4, decoder_7_out5, decoder_7_out6, decoder_7_out7, decoder_7_out8, decoder_7_out9);
  Transistor transistor_4 (.in(subtractor_1_bout), .out(transistor_4_out), .gate(and_3_out[3]));
  Transistor #(.gate("br")) transistor_5 (.in(transistor_4_out), .out(transistor_5_out), .gate(and_3_out[1]));
  Transistor #(.gate("br")) transistor_6 (.in(transistor_5_out), .out(transistor_6_out), .gate(and_3_out[0]));
  D_Flip_Flop d_ff_7 (.clk(d_ff_6_q), .D(d_ff_5_qn[2]), .Q(d_ff_7_q), .Qn(d_ff_5_qn[2]));  // open: preset, en, reset
  Decoder #(.select(4)) decoder_7 (
    .out0(decoder_7_out0), .out1(decoder_7_out1), .out2(decoder_7_out2), .out3(decoder_7_out3),
    .out4(decoder_7_out4), .out5(decoder_7_out5), .out6(decoder_7_out6), .out7(decoder_7_out7),
    .out8(decoder_7_out8), .out9(decoder_7_out9), .out10(decoder_7_out10), .out11(decoder_7_out11),
    .out12(decoder_7_out12), .out13(decoder_7_out13), .out14(decoder_7_out14), .out15(decoder_7_out15),
    .sel(d_ff_5_qn), .en(1'b1));
  or BR (BR_out[0], _0_out, _1_out, _3_out, _4_out, _5_out, _6_out, _7_out, _8_out, _9_out);
  or B (BR_out[1], _0_out, _2_out, _3_out, _5_out, _6_out, _8_out, _9_out);
  or BL (BR_out[2], _0_out, _2_out, _6_out, _8_out);
  or TR (TR_out[0], _0_out, _1_out, _2_out, _3_out, _4_out, _7_out, _8_out, _9_out);
  or T (TR_out[1], _0_out, _2_out, _3_out, _5_out, _6_out, _7_out, _8_out, _9_out);
  or TL (TR_out[2], _0_out, _4_out, _5_out, _6_out, _8_out, _9_out);
  or C (TR_out[3], _2_out, _3_out, _4_out, _5_out, _6_out, _8_out, _9_out);
  Decoder #(.select(4)) decoder_8 (
    .out0(decoder_8_out0[0]), .out1(decoder_8_out0[1]), .out2(decoder_8_out0[2]), .out3(decoder_8_out0[3]),
    .out4(decoder_8_out0[4]), .out5(decoder_8_out0[5]), .out6(decoder_8_out0[6]), .out7(decoder_8_out0[7]),
    .out8(decoder_8_out0[8]), .out9(decoder_8_out0[9]), .out10(decoder_8_out0[10]),
    .out11(decoder_8_out0[11]), .out12(decoder_8_out0[12]), .out13(decoder_8_out0[13]),
    .out14(decoder_8_out0[14]), .out15(decoder_8_out0[15]), .sel(multiplier_1_out), .en(decoder_3_out0));
  Decoder #(.select(4)) decoder_9 (
    .out0(decoder_9_out0[0]), .out1(decoder_9_out0[1]), .out2(decoder_9_out0[2]), .out3(decoder_9_out0[3]),
    .out4(decoder_9_out0[4]), .out5(decoder_9_out0[5]), .out6(decoder_9_out0[6]), .out7(decoder_9_out0[7]),
    .out8(decoder_9_out0[8]), .out9(decoder_9_out0[9]), .out10(decoder_9_out0[10]),
    .out11(decoder_9_out0[11]), .out12(decoder_9_out0[12]), .out13(decoder_9_out0[13]),
    .out14(decoder_9_out0[14]), .out15(decoder_9_out0[15]), .sel(multiplier_1_out), .en(decoder_3_out1));
  Decoder #(.select(4)) decoder_10 (
    .out0(decoder_10_out0[0]), .out1(decoder_10_out0[1]), .out2(decoder_10_out0[2]),
    .out3(decoder_10_out0[3]), .out4(decoder_10_out0[4]), .out5(decoder_10_out0[5]),
    .out6(decoder_10_out0[6]), .out7(decoder_10_out0[7]), .out8(decoder_10_out0[8]),
    .out9(decoder_10_out0[9]), .out10(decoder_10_out0[10]), .out11(decoder_10_out0[11]),
    .out12(decoder_10_out0[12]), .out13(decoder_10_out0[13]), .out14(decoder_10_out0[14]),
    .out15(decoder_10_out0[15]), .sel(multiplier_1_out), .en(decoder_3_out2));
  Decoder #(.select(4)) decoder_11 (
    .out0(decoder_11_out0[0]), .out1(decoder_11_out0[1]), .out2(decoder_11_out0[2]),
    .out3(decoder_11_out0[3]), .out4(decoder_11_out0[4]), .out5(decoder_11_out0[5]),
    .out6(decoder_11_out0[6]), .out7(decoder_11_out0[7]), .out8(decoder_11_out0[8]),
    .out9(decoder_11_out0[9]), .out10(decoder_11_out0[10]), .out11(decoder_11_out0[11]),
    .out12(decoder_11_out0[12]), .out13(decoder_11_out0[13]), .out14(decoder_11_out0[14]),
    .out15(decoder_11_out0[15]), .sel(multiplier_1_out), .en(decoder_3_out3));
  Decoder #(.select(4)) decoder_12 (
    .out0(decoder_12_out0[0]), .out1(decoder_12_out0[1]), .out2(decoder_12_out0[2]),
    .out3(decoder_12_out0[3]), .out4(decoder_12_out0[4]), .out5(decoder_12_out0[5]),
    .out6(decoder_12_out0[6]), .out7(decoder_12_out0[7]), .out8(decoder_12_out0[8]),
    .out9(decoder_12_out0[9]), .out10(decoder_12_out0[10]), .out11(decoder_12_out0[11]),
    .out12(decoder_12_out0[12]), .out13(decoder_12_out0[13]), .out14(decoder_12_out0[14]),
    .out15(decoder_12_out0[15]), .sel(multiplier_1_out), .en(decoder_3_out4));
  Decoder #(.select(4)) decoder_13 (
    .out0(decoder_13_out0[0]), .out1(decoder_13_out0[1]), .out2(decoder_13_out0[2]),
    .out3(decoder_13_out0[3]), .out4(decoder_13_out0[4]), .out5(decoder_13_out0[5]),
    .out6(decoder_13_out0[6]), .out7(decoder_13_out0[7]), .out8(decoder_13_out0[8]),
    .out9(decoder_13_out0[9]), .out10(decoder_13_out0[10]), .out11(decoder_13_out0[11]),
    .out12(decoder_13_out0[12]), .out13(decoder_13_out0[13]), .out14(decoder_13_out0[14]),
    .out15(decoder_13_out0[15]), .sel(multiplier_1_out), .en(decoder_3_out5));
  Decoder #(.select(4)) decoder_14 (
    .out0(decoder_14_out0[0]), .out1(decoder_14_out0[1]), .out2(decoder_14_out0[2]),
    .out3(decoder_14_out0[3]), .out4(decoder_14_out0[4]), .out5(decoder_14_out0[5]),
    .out6(decoder_14_out0[6]), .out7(decoder_14_out0[7]), .out8(decoder_14_out0[8]),
    .out9(decoder_14_out0[9]), .out10(decoder_14_out0[10]), .out11(decoder_14_out0[11]),
    .out12(decoder_14_out0[12]), .out13(decoder_14_out0[13]), .out14(decoder_14_out0[14]),
    .out15(decoder_14_out0[15]), .sel(multiplier_1_out), .en(decoder_3_out6));
  Decoder #(.select(4)) decoder_15 (
    .out0(decoder_15_out0[0]), .out1(decoder_15_out0[1]), .out2(decoder_15_out0[2]),
    .out3(decoder_15_out0[3]), .out4(decoder_15_out0[4]), .out5(decoder_15_out0[5]),
    .out6(decoder_15_out0[6]), .out7(decoder_15_out0[7]), .out8(decoder_15_out0[8]),
    .out9(decoder_15_out0[9]), .out10(decoder_15_out0[10]), .out11(decoder_15_out0[11]),
    .out12(decoder_15_out0[12]), .out13(decoder_15_out0[13]), .out14(decoder_15_out0[14]),
    .out15(decoder_15_out0[15]), .sel(multiplier_1_out), .en(decoder_3_out7));
  Decoder #(.select(4)) decoder_16 (
    .out0(decoder_16_out0[0]), .out1(decoder_16_out0[1]), .out2(decoder_16_out0[2]),
    .out3(decoder_16_out0[3]), .out4(decoder_16_out0[4]), .out5(decoder_16_out0[5]),
    .out6(decoder_16_out0[6]), .out7(decoder_16_out0[7]), .out8(decoder_16_out0[8]),
    .out9(decoder_16_out0[9]), .out10(decoder_16_out0[10]), .out11(decoder_16_out0[11]),
    .out12(decoder_16_out0[12]), .out13(decoder_16_out0[13]), .out14(decoder_16_out0[14]),
    .out15(decoder_16_out0[15]), .sel(multiplier_1_out), .en(decoder_3_out8));
  Decoder #(.select(4)) decoder_17 (
    .out0(decoder_17_out0[0]), .out1(decoder_17_out0[1]), .out2(decoder_17_out0[2]),
    .out3(decoder_17_out0[3]), .out4(decoder_17_out0[4]), .out5(decoder_17_out0[5]),
    .out6(decoder_17_out0[6]), .out7(decoder_17_out0[7]), .out8(decoder_17_out0[8]),
    .out9(decoder_17_out0[9]), .out10(decoder_17_out0[10]), .out11(decoder_17_out0[11]),
    .out12(decoder_17_out0[12]), .out13(decoder_17_out0[13]), .out14(decoder_17_out0[14]),
    .out15(decoder_17_out0[15]), .sel(multiplier_1_out), .en(decoder_3_out9));
  Decoder #(.select(4)) decoder_18 (
    .out0(decoder_18_out0[0]), .out1(decoder_18_out0[1]), .out2(decoder_18_out0[2]),
    .out3(decoder_18_out0[3]), .out4(decoder_18_out0[4]), .out5(decoder_18_out0[5]),
    .out6(decoder_18_out0[6]), .out7(decoder_18_out0[7]), .out8(decoder_18_out0[8]),
    .out9(decoder_18_out0[9]), .out10(decoder_18_out0[10]), .out11(decoder_18_out0[11]),
    .out12(decoder_18_out0[12]), .out13(decoder_18_out0[13]), .out14(decoder_18_out0[14]),
    .out15(decoder_18_out0[15]), .sel(multiplier_1_out), .en(decoder_3_out10));
  Decoder #(.select(4)) decoder_19 (
    .out0(decoder_18_out0[16]), .out1(decoder_18_out0[17]), .out2(decoder_18_out0[18]),
    .out3(decoder_18_out0[19]), .out4(decoder_18_out0[20]), .out5(decoder_18_out0[21]),
    .out6(decoder_18_out0[22]), .out7(decoder_18_out0[23]), .out8(decoder_18_out0[24]),
    .out9(decoder_18_out0[25]), .out10(decoder_18_out0[26]), .out11(decoder_18_out0[27]),
    .out12(decoder_18_out0[28]), .out13(decoder_18_out0[29]), .out14(decoder_18_out0[30]),
    .out15(decoder_18_out0[31]), .sel(multiplier_1_out), .en(decoder_3_out11));
  Decoder #(.select(4)) decoder_20 (
    .out0(decoder_20_out0[0]), .out1(decoder_20_out0[1]), .out2(decoder_20_out0[2]),
    .out3(decoder_20_out0[3]), .out4(decoder_20_out0[4]), .out5(decoder_20_out0[5]),
    .out6(decoder_20_out0[6]), .out7(decoder_20_out0[7]), .out8(decoder_20_out0[8]),
    .out9(decoder_20_out0[9]), .out10(decoder_20_out0[10]), .out11(decoder_20_out0[11]),
    .out12(decoder_20_out0[12]), .out13(decoder_20_out0[13]), .out14(decoder_20_out0[14]),
    .out15(decoder_20_out0[15]), .sel(multiplier_1_out), .en(decoder_3_out12));
  Decoder #(.select(4)) decoder_21 (
    .out0(decoder_21_out0[0]), .out1(decoder_21_out0[1]), .out2(decoder_21_out0[2]),
    .out3(decoder_21_out0[3]), .out4(decoder_21_out0[4]), .out5(decoder_21_out0[5]),
    .out6(decoder_21_out0[6]), .out7(decoder_21_out0[7]), .out8(decoder_21_out0[8]),
    .out9(decoder_21_out0[9]), .out10(decoder_21_out0[10]), .out11(decoder_21_out0[11]),
    .out12(decoder_21_out0[12]), .out13(decoder_21_out0[13]), .out14(decoder_21_out0[14]),
    .out15(decoder_21_out0[15]), .sel(multiplier_1_out), .en(decoder_3_out13));
  Decoder #(.select(4)) decoder_22 (
    .out0(decoder_22_out0[0]), .out1(decoder_22_out0[1]), .out2(decoder_22_out0[2]),
    .out3(decoder_22_out0[3]), .out4(decoder_22_out0[4]), .out5(decoder_22_out0[5]),
    .out6(decoder_22_out6[0]), .out7(decoder_22_out6[1]), .out8(decoder_22_out6[2]),
    .out9(decoder_22_out6[3]), .out10(decoder_22_out0[10]), .out11(decoder_22_out0[11]),
    .out12(decoder_22_out0[12]), .out13(decoder_22_out0[13]), .out14(decoder_22_out0[14]),
    .out15(decoder_22_out0[15]), .sel(multiplier_1_out), .en(decoder_3_out14));
  D_Flip_Flop d_ff_8 (.clk(d_ff_7_q), .D(d_ff_5_qn[3]), .Qn(d_ff_5_qn[3]));  // open: Q, preset, en, reset
  D_Flip_Flop d_ff_9 (.clk(_2_3_out[1]), .D(d_ff_9_qn), .Q(d_ff_9_q), .Qn(d_ff_9_qn));  // open: preset, en, reset
  and \and  (and_3_out[2], ~d_ff_9_qn, ~d_ff_10_qn);  // AND_Gate
  and and_2 (and_3_out[3], d_ff_10_qn, d_ff_9_qn);
  or _2_1X_2 (_2_0X_2_out[1], decoder_7_out10, decoder_7_out11, decoder_7_out12, decoder_7_out13, decoder_7_out14, decoder_7_out15);
  or _0_2 (_0_2_out, decoder_7_out0, decoder_7_out10);
  or _1_2 (_1_2_out, decoder_7_out1, decoder_7_out11);
  or _2_2 (_2_2_out, decoder_7_out2, decoder_7_out12);
  or _3_2 (_3_2_out, decoder_7_out3, decoder_7_out13);
  or _4_2 (_4_2_out, decoder_7_out4, decoder_7_out14);
  or _5_2 (_5_2_out, decoder_7_out5, decoder_7_out15);
  buf _6_2 (_6_2_out, decoder_7_out6);
  buf _7_2 (_7_2_out, decoder_7_out7);
  buf _8_2 (_8_2_out, decoder_7_out8);
  buf _9_2 (_9_2_out, decoder_7_out9);
  D_Flip_Flop d_ff_10 (.clk(d_ff_9_q), .D(d_ff_10_qn), .Qn(d_ff_10_qn));  // open: Q, preset, en, reset
  and and_3 (and_3_out[0], ~d_ff_9_qn, d_ff_10_qn);  // AND_Gate
  and and_4 (and_3_out[1], d_ff_9_qn, ~d_ff_10_qn);  // AND_Gate
  buf B_2 (BR_3_out[1], _2_0X_2_out[0]);
  buf BL_2 (BR_3_out[2], _2_0X_2_out[0]);
  buf T_2 (TR_3_out[1], _2_0X_2_out[0]);
  buf TL_2 (TR_3_out[2], _2_0X_2_out[0]);
  assign {Sign_out_4, Sign_out_3, Sign_out_2, Sign_out} = transistor_8_out | transistor_7_out | transistor_11_out | transistor_10_out;  // OR_Gate Sign, 25 bits wide
  Transistor #(.\type ("n"), .width(25)) transistor_7 (
    .in({undriven_5[24:23], 1'b1, undriven_5[21:18], 1'b1, undriven_5[16:13], 1'b1, undriven_5[11:8], 1'b1, undriven_5[6:3], 1'b1, undriven_5[1:0]}),
    .out(transistor_7_out), .gate(and_3_out[2]));
  Transistor #(.\type ("n"), .width(25)) transistor_8 (
    .in({undriven_2[24:23], 1'b1, undriven_2[21:18], 1'b1, undriven_2[16:15], {5{1'b1}}, undriven_2[9:8], 1'b1, undriven_2[6:3], 1'b1, undriven_2[1:0]}),
    .out(transistor_8_out), .gate(and_3_out[3]));
  or BR_2 (BR_2_out[0], _2_0X_out[0], _2_0X_out[1]);
  buf B_3 (BR_2_out[1], _2_0X_out[0]);
  buf BL_3 (BR_2_out[2], _2_0X_out[0]);
  or TR_2 (BR_2_out[3], _2_0X_out[0], _2_0X_out[1]);
  buf T_3 (BR_2_out[4], _2_0X_out[0]);
  buf TL_3 (BR_2_out[5], _2_0X_out[0]);
  or BR_3 (BR_3_out[0], _2_0X_2_out[0], _2_0X_2_out[1]);
  or TR_3 (TR_3_out[0], _2_0X_2_out[0], _2_0X_2_out[1]);
  or BR_4 (BR_4_out[0], _0_2_out, _1_2_out, _3_2_out, _4_2_out, _5_2_out, _6_2_out, _7_2_out, _8_2_out, _9_2_out);
  or B_4 (BR_4_out[1], _0_2_out, _2_2_out, _3_2_out, _5_2_out, _6_2_out, _8_2_out, _9_2_out);
  or BL_4 (BR_4_out[2], _0_2_out, _2_2_out, _6_2_out, _8_2_out);
  or TR_4 (BR_4_out[3], _0_2_out, _1_2_out, _2_2_out, _3_2_out, _4_2_out, _7_2_out, _8_2_out, _9_2_out);
  or T_4 (BR_4_out[4], _0_2_out, _2_2_out, _3_2_out, _5_2_out, _6_2_out, _7_2_out, _8_2_out, _9_2_out);
  Transistor #(.width(31)) transistor_9 (.in({undriven, MN_2_out}), .out(transistor_9_out), .gate(_0ERR_out));
  or TL_4 (BR_4_out[5], _0_2_out, _4_2_out, _5_2_out, _6_2_out, _8_2_out, _9_2_out);
  or C_2 (BR_4_out[6], _2_2_out, _3_2_out, _4_2_out, _5_2_out, _6_2_out, _8_2_out, _9_2_out);
  Transistor #(.\type ("n"), .width(25)) transistor_10 (
    .in({undriven_4[24:23], 1'b1, undriven_4[21:18], 1'b1, undriven_4[16:15], 1'b1, undriven_4[13], 1'b1, undriven_4[11], 1'b1, undriven_4[9:8], 1'b1, undriven_4[6:3], 1'b1, undriven_4[1:0]}),
    .out(transistor_10_out), .gate(and_3_out[0]));
  Transistor #(.\type ("n"), .width(25)) transistor_11 (
    .in({1'b1, undriven_3[23:21], 1'b1, undriven_3[19], 1'b1, undriven_3[17], 1'b1, undriven_3[15:13], 1'b1, undriven_3[11:9], 1'b1, undriven_3[7], 1'b1, undriven_3[5], 1'b1, undriven_3[3:1], 1'b1}),
    .out(transistor_11_out), .gate(and_3_out[1]));
  and _0ERR (_0ERR_out, decoder_7_out0, and_3_out[0]);
  assign {P_X0X_out[3], PM_out} = transistor_9_out | decoder_1_out0;  // OR_Gate PM, 31 bits wide
  or X_XX0 (X_XX0_out[0], decoder_8_out0[0], decoder_8_out0[10], decoder_9_out0[4], decoder_9_out0[14]);
  or X_XX1 (X_XX0_2_out[1], decoder_10_out0[9], decoder_11_out0[3], decoder_11_out0[13]);
  or X_XX0_2 (X_XX0_2_out[0], decoder_10_out0[8], decoder_11_out0[2], decoder_11_out0[12]);
  _7_Segment_Display u_7_segment_display_1 (
    .g(1'b0), .f(BR_2_out[5]), .a(BR_2_out[4]), .b(BR_2_out[3]), .e(BR_2_out[2]), .d(BR_2_out[1]),
    .c(BR_2_out[0]));  // open: dp
  _7_Segment_Display u_7_segment_display_2 (
    .g(TR_out[3]), .f(TR_out[2]), .a(TR_out[1]), .b(TR_out[0]), .e(BR_out[2]), .d(BR_out[1]), .c(BR_out[0]));  // open: dp
  or P_X2X (P_X0X_out[2], PM_out[29], PM_out[28], PM_out[27], PM_out[26], PM_out[25], PM_out[24], PM_out[23], PM_out[22], PM_out[21], PM_out[20]);
  or X_XX2 (X_XX0_out[2], decoder_8_out0[2], decoder_8_out0[12], decoder_9_out0[6]);
  or X_XX1_2 (X_XX0_out[1], decoder_8_out0[1], decoder_8_out0[11], decoder_9_out0[5], decoder_9_out0[15]);
  or X_XX2_2 (X_XX0_2_out[2], decoder_10_out0[0], decoder_10_out0[10], decoder_11_out0[4], decoder_11_out0[14]);
  or X_XX3 (X_XX0_2_out[3], decoder_10_out0[1], decoder_10_out0[11], decoder_11_out0[5], decoder_11_out0[15]);
  DotMatrix #(.matrixrows(5)) dotmatrix_1 (
    .col0(Sign_out_4), .col1(Sign_out_3), .col2(Sign_out_2), .col3(Sign_out[9:5]), .col4(Sign_out[4:0]));
  or _0_Check (_0_Check_out, transistor_12_out, transistor_13_out);
  Transistor transistor_12 (.in(P_0XX_out), .out(transistor_12_out), .gate(transistor_6_out));
  or P_X1X (P_X0X_out[1], PM_out[19], PM_out[18], PM_out[17], PM_out[16], PM_out[15], PM_out[14], PM_out[13], PM_out[12], PM_out[11], PM_out[10]);
  or P_0XX (P_0XX_out, P_X0X_out[3], PM_out[29], PM_out[28], PM_out[27], PM_out[26], PM_out[25], PM_out[24], PM_out[23], PM_out[22], PM_out[21], PM_out[20], PM_out[19], PM_out[18], PM_out[17], PM_out[16], PM_out[15], PM_out[14], PM_out[13], PM_out[12], PM_out[11], PM_out[10], PM_out[9], PM_out[8], PM_out[7], PM_out[6], PM_out[5], PM_out[4], PM_out[3], PM_out[2], PM_out[1], PM_out[0]);
  or X_XX4 (X_XX0_out[4], decoder_8_out0[4], decoder_8_out0[14], decoder_9_out0[8]);
  or X_XX3_2 (X_XX0_out[3], decoder_8_out0[3], decoder_8_out0[13], decoder_9_out0[7]);
  or X_XX5 (X_XX5_out[0], decoder_8_out0[5], decoder_8_out0[15], decoder_9_out0[9]);
  or X_XX5_2 (X_XX5_2_out[5], decoder_10_out0[3], decoder_10_out0[13], decoder_11_out0[7]);
  or X_XX4_2 (X_XX0_2_out[4], decoder_10_out0[2], decoder_10_out0[12], decoder_11_out0[6]);
  _7_Segment_Display u_7_segment_display_3 (
    .g(BR_4_out[6]), .f(BR_4_out[5]), .a(BR_4_out[4]), .b(BR_4_out[3]), .e(BR_4_out[2]), .d(BR_4_out[1]),
    .c(BR_4_out[0]));  // open: dp
  _7_Segment_Display u_7_segment_display_4 (
    .g(1'b0), .f(TR_3_out[2]), .a(TR_3_out[1]), .b(TR_3_out[0]), .e(BR_3_out[2]), .d(BR_3_out[1]),
    .c(BR_3_out[0]));  // open: dp
  or BR_5 (BR_5_out[0], Hundreds_out, X_0XX_2_out[1]);
  or B_5 (BR_5_out[1], Hundreds_out, _0ERR_out, X_0XX_2_out[2]);
  or BL_5 (BR_5_out[2], Hundreds_out, _0ERR_out, X_0XX_2_out[2]);
  or TR_5 (TR_5_out[0], Hundreds_out, X_0XX_2_out[1], X_0XX_2_out[2]);
  or T_5 (TR_5_out[1], Hundreds_out, _0ERR_out, X_0XX_2_out[2]);
  or TL_5 (TR_5_out[2], Hundreds_out, _0ERR_out);
  or C_3 (TR_5_out[3], X_0XX_2_out[2], _0ERR_out, transistor_6_out);
  or Hundreds (Hundreds_out, X_0XX_2_out[0], Hundreds_2_out);
  or Hundreds_2 (Hundreds_2_out, _0_Check_out, Check_out);
  and Check (Check_out, and_3_out[3], P_0XX_out);
  Transistor #(.gate("br")) transistor_13 (.in(and_3_out[0]), .out(transistor_13_out), .gate(_0ERR_out));
  or P_X0X (P_X0X_out[0], PM_out[9], PM_out[8], PM_out[7], PM_out[6], PM_out[5], PM_out[4], PM_out[3], PM_out[2], PM_out[1], PM_out[0]);
  or X_XX7 (X_XX5_out[2], decoder_8_out0[7], decoder_9_out0[1], decoder_9_out0[11]);
  or X_XX8 (X_XX5_out[3], decoder_8_out0[8], decoder_9_out0[2], decoder_9_out0[12]);
  or X_XX6 (X_XX5_out[1], decoder_8_out0[6], decoder_9_out0[0], decoder_9_out0[10]);
  or X_XX6_2 (X_XX5_2_out[6], decoder_10_out0[4], decoder_10_out0[14], decoder_11_out0[8]);
  or X_XX8_2 (X_XX5_2_out[8], decoder_10_out0[6], decoder_11_out0[0], decoder_11_out0[10]);
  or X_XX7_2 (X_XX5_2_out[7], decoder_10_out0[5], decoder_10_out0[15], decoder_11_out0[9]);
  DotMatrix #(.matrixrows(5)) dotmatrix_2 (
    .col0({undriven_9[4], 1'b1, undriven_9[2], 1'b1, undriven_9[0]}),
    .col1({undriven_8[4], 1'b1, undriven_8[2], 1'b1, undriven_8[0]}),
    .col2({undriven_7[4], 1'b1, undriven_7[2], 1'b1, undriven_7[0]}),
    .col3({undriven_6[9], 1'b1, undriven_6[7], 1'b1, undriven_6[5]}),
    .col4({undriven_6[4], 1'b1, undriven_6[2], 1'b1, undriven_6[0]}));
  or P_XX9 (P_XX0_out[9], PM_out[29], PM_out[19], PM_out[9]);
  or P_XX8 (P_XX0_out[8], PM_out[28], PM_out[18], PM_out[8]);
  or P_XX7 (P_XX0_out[7], PM_out[27], PM_out[17], PM_out[7]);
  or P_XX6 (P_XX0_out[6], PM_out[26], PM_out[16], PM_out[6]);
  or P_XX5 (P_XX0_out[5], PM_out[25], PM_out[15], PM_out[5]);
  or P_XX4 (P_XX0_out[4], PM_out[24], PM_out[14], PM_out[4]);
  or P_XX3 (P_XX0_out[3], PM_out[23], PM_out[13], PM_out[3]);
  or P_XX2 (P_XX0_out[2], PM_out[22], PM_out[12], PM_out[2]);
  or P_XX1 (P_XX0_out[1], PM_out[21], PM_out[11], PM_out[1]);
  or P_XX0 (P_XX0_out[0], P_X0X_out[3], PM_out[20], PM_out[10], PM_out[0]);
  or X_XX9 (X_XX5_out[4], decoder_8_out0[9], decoder_9_out0[3], decoder_9_out0[13]);
  or X_XX9_2 (X_XX5_2_out[9], decoder_10_out0[7], decoder_11_out0[1], decoder_11_out0[11]);
  _7_Segment_Display u_7_segment_display_5 (
    .g(TR_5_out[3]), .f(TR_5_out[2]), .a(TR_5_out[1]), .b(TR_5_out[0]), .e(BR_5_out[2]), .d(BR_5_out[1]),
    .c(BR_5_out[0]));  // open: dp
  _7_Segment_Display u_7_segment_display_6 (
    .g(TR_6_out[3]), .f(TR_6_out[2]), .a(TR_6_out[1]), .b(TR_6_out[0]), .e(BR_6_out[2]), .d(BR_6_out[1]),
    .c(BR_6_out[0]));  // open: dp
  or BR_6 (BR_6_out[0], Tens_out[0], Tens_out[1], Tens_out[3], Tens_out[4], Tens_out[5], Tens_out[6], Tens_out[7], Tens_out[8], Tens_out[9]);
  or B_6 (BR_6_out[1], Tens_out[0], Tens_out[2], Tens_out[3], Tens_out[5], Tens_out[6], Tens_out[8], Tens_out[9]);
  or BL_6 (BR_6_out[2], Tens_out[0], Tens_out[2], Tens_out[6], Tens_out[8]);
  or TR_6 (TR_6_out[0], Tens_out[0], Tens_out[1], Tens_out[2], Tens_out[3], Tens_out[4], Tens_out[7], Tens_out[8], Tens_out[9]);
  or T_6 (TR_6_out[1], Tens_out[0], Tens_out[2], Tens_out[3], Tens_out[5], Tens_out[6], Tens_out[7], Tens_out[8], Tens_out[9]);
  or TL_6 (TR_6_out[2], Tens_out[0], Tens_out[4], Tens_out[5], Tens_out[6], Tens_out[8], Tens_out[9]);
  or C_4 (TR_6_out[3], Tens_out[2], Tens_out[3], Tens_out[4], Tens_out[5], Tens_out[6], Tens_out[8], Tens_out[9]);
  or X_X0X (X_X0X_out[0], decoder_8_out0[0], decoder_8_out0[1], decoder_8_out0[2], decoder_8_out0[3], decoder_8_out0[4], decoder_8_out0[5], decoder_8_out0[6], decoder_8_out0[7], decoder_8_out0[8], decoder_8_out0[9]);
  or X_X3X (X_X3X_out, decoder_10_out0[0], decoder_10_out0[1], decoder_10_out0[2], decoder_10_out0[3], decoder_10_out0[4], decoder_10_out0[5], decoder_10_out0[6], decoder_10_out0[7]);
  or X_X4X (X_X4X_out[0], decoder_10_out0[8], decoder_10_out0[9], decoder_10_out0[10], decoder_10_out0[11], decoder_10_out0[12], decoder_10_out0[13], decoder_10_out0[14], decoder_10_out0[15], decoder_11_out0[0], decoder_11_out0[1]);
  or X_X6X (X_X4X_out[2], decoder_11_out0[12], decoder_11_out0[13], decoder_11_out0[14], decoder_11_out0[15], X_X6X_2_out);
  _7_Segment_Display u_7_segment_display_7 (
    .g(TR_7_out[3]), .f(TR_7_out[2]), .a(TR_7_out[1]), .b(TR_7_out[0]), .e(BR_7_out[2]), .d(BR_7_out[1]),
    .c(BR_7_out[0]));  // open: dp
  assign Tens_out = P_X0X_out | Tens_2_out;  // OR_Gate Tens, 10 bits wide
  assign Mult_Ones_out = {X_XX5_out, X_XX0_out} | {X_XX5_2_out, X_XX0_2_out} | X_XX0_4_out | X_XX0_5_out | X_XX0_3_out | X_XX0_6_out | X_XX0_7_out | decoder_22_out6;  // OR_Gate Mult_Ones, 10 bits wide
  or X_0XX (X_0XX_out, X_X0X_out[0], X_X0X_out[1], X_X0X_out[2], X_X0X_out[3]);
  or X_X1X (X_X0X_out[1], decoder_8_out0[10], decoder_8_out0[11], decoder_8_out0[12], decoder_8_out0[13], decoder_8_out0[14], decoder_8_out0[15], decoder_9_out0[0], decoder_9_out0[1], decoder_9_out0[2], decoder_9_out0[3]);
  or X_X2X (X_X0X_out[2], decoder_9_out0[4], decoder_9_out0[5], decoder_9_out0[6], decoder_9_out0[7], decoder_9_out0[8], decoder_9_out0[9], decoder_9_out0[10], decoder_9_out0[11], decoder_9_out0[12], decoder_9_out0[13]);
  or X_X3X_2 (X_X0X_out[3], decoder_9_out0[14], decoder_9_out0[15], X_X3X_out);
  or X_X5X (X_X4X_out[1], decoder_11_out0[2], decoder_11_out0[3], decoder_11_out0[4], decoder_11_out0[5], decoder_11_out0[6], decoder_11_out0[7], decoder_11_out0[8], decoder_11_out0[9], decoder_11_out0[10], decoder_11_out0[11]);
  Button F (.out(_2_3_out[1]));
  Button _2_3 (.out(_2_3_out[0]));
  Button _1_3 (.out(_2_3_out[2]));
  assign Tens_2_out = {X_X4X_out, X_X0X_out} | Tens_3_out;  // OR_Gate Tens_2, 10 bits wide
  assign Ones_out = P_XX0_out | Mult_Ones_out;  // OR_Gate Ones, 10 bits wide
  or X_0XX_2 (X_0XX_2_out[0], X_0XX_out, X_0XX_3_out, X_0XX_4_out);
  or X_0XX_3 (X_0XX_3_out, X_X3X_out, X_X4X_out[0], X_X4X_out[1], X_X4X_out[2]);
  or BR_7 (BR_7_out[0], Ones_out[0], Ones_out[1], Ones_out[3], Ones_out[4], Ones_out[5], Ones_out[6], Ones_out[7], Ones_out[8], Ones_out[9]);
  or B_7 (BR_7_out[1], Ones_out[0], Ones_out[2], Ones_out[3], Ones_out[5], Ones_out[6], Ones_out[8], Ones_out[9]);
  or BL_7 (BR_7_out[2], Ones_out[0], Ones_out[2], Ones_out[6], Ones_out[8]);
  or TR_7 (TR_7_out[0], Ones_out[0], Ones_out[1], Ones_out[2], Ones_out[3], Ones_out[4], Ones_out[7], Ones_out[8], Ones_out[9]);
  or T_7 (TR_7_out[1], Ones_out[0], Ones_out[2], Ones_out[3], Ones_out[5], Ones_out[6], Ones_out[7], Ones_out[8], Ones_out[9]);
  or TL_7 (TR_7_out[2], Ones_out[0], Ones_out[4], Ones_out[5], Ones_out[6], Ones_out[8], Ones_out[9]);
  or C_5 (TR_7_out[3], Ones_out[2], Ones_out[3], Ones_out[4], Ones_out[5], Ones_out[6], Ones_out[8], Ones_out[9]);
  or X_XX0_3 (X_XX0_3_out[0], decoder_16_out0[2], decoder_16_out0[12], decoder_17_out0[6]);
  or X_XX1_3 (X_XX0_3_out[1], decoder_16_out0[3], decoder_16_out0[13], decoder_17_out0[7]);
  or X_XX0_4 (X_XX0_4_out[0], decoder_12_out0[6], decoder_13_out0[0], decoder_13_out0[10]);
  or X_XX0_5 (X_XX0_5_out[0], decoder_14_out0[4], decoder_14_out0[14], decoder_15_out0[8]);
  or X_XX2_3 (X_XX0_3_out[2], decoder_16_out0[4], decoder_16_out0[14], decoder_17_out0[8]);
  or X_XX3_3 (X_XX0_3_out[3], decoder_16_out0[5], decoder_16_out0[15], decoder_17_out0[9]);
  or X_XX3_4 (X_XX0_4_out[3], decoder_12_out0[9], decoder_13_out0[3], decoder_13_out0[13]);
  or X_XX2_4 (X_XX0_4_out[2], decoder_12_out0[8], decoder_13_out0[2], decoder_13_out0[12]);
  or X_XX1_4 (X_XX0_4_out[1], decoder_12_out0[7], decoder_13_out0[1], decoder_13_out0[11]);
  or X_XX3_5 (X_XX0_5_out[3], decoder_14_out0[7], decoder_15_out0[1], decoder_15_out0[11]);
  or X_XX1_5 (X_XX0_5_out[1], decoder_14_out0[5], decoder_14_out0[15], decoder_15_out0[9]);
  or X_XX2_5 (X_XX0_5_out[2], decoder_14_out0[6], decoder_15_out0[0], decoder_15_out0[10]);
  or X_XX4_3 (X_XX0_3_out[4], decoder_16_out0[6], decoder_17_out0[0], decoder_17_out0[10]);
  or X_XX6_3 (X_XX0_3_out[6], decoder_16_out0[8], decoder_17_out0[2], decoder_17_out0[12]);
  or X_XX5_3 (X_XX0_3_out[5], decoder_16_out0[7], decoder_17_out0[1], decoder_17_out0[11]);
  or X_XX4_4 (X_XX0_4_out[4], decoder_12_out0[0], decoder_12_out0[10], decoder_13_out0[4], decoder_13_out0[14]);
  or X_XX5_4 (X_XX0_5_out[5], decoder_14_out0[9], decoder_15_out0[3], decoder_15_out0[13]);
  or X_XX4_5 (X_XX0_5_out[4], decoder_14_out0[8], decoder_15_out0[2], decoder_15_out0[12]);
  or X_XX7_3 (X_XX0_3_out[7], decoder_16_out0[9], decoder_17_out0[3], decoder_17_out0[13]);
  or X_XX8_3 (X_XX0_3_out[8], decoder_16_out0[0], decoder_16_out0[10], decoder_17_out0[4], decoder_17_out0[14]);
  or X_XX6_4 (X_XX0_4_out[6], decoder_12_out0[2], decoder_12_out0[12], decoder_13_out0[6]);
  or X_XX7_4 (X_XX0_4_out[7], decoder_12_out0[3], decoder_12_out0[13], decoder_13_out0[7]);
  or X_XX5_5 (X_XX0_4_out[5], decoder_12_out0[1], decoder_12_out0[11], decoder_13_out0[5], decoder_13_out0[15]);
  or X_XX7_5 (X_XX0_5_out[7], decoder_14_out0[1], decoder_14_out0[11], decoder_15_out0[5], decoder_15_out0[15]);
  or X_XX6_5 (X_XX0_5_out[6], decoder_14_out0[0], decoder_14_out0[10], decoder_15_out0[4], decoder_15_out0[14]);
  or X_XX9_3 (X_XX0_3_out[9], decoder_16_out0[1], decoder_16_out0[11], decoder_17_out0[5], decoder_17_out0[15]);
  or X_XX9_4 (X_XX0_4_out[9], decoder_12_out0[5], decoder_12_out0[15], decoder_13_out0[9]);
  or X_XX8_4 (X_XX0_4_out[8], decoder_12_out0[4], decoder_12_out0[14], decoder_13_out0[8]);
  or X_XX8_5 (X_XX0_5_out[8], decoder_14_out0[2], decoder_14_out0[12], decoder_15_out0[6]);
  or X_XX9_5 (X_XX0_5_out[9], decoder_14_out0[3], decoder_14_out0[13], decoder_15_out0[7]);
  or X_X2X_2 (X_X2X_2_out[0], decoder_16_out0[0], decoder_16_out0[1]);
  or X_X3X_3 (X_X3X_3_out, decoder_16_out0[2], decoder_16_out0[3], decoder_16_out0[4], decoder_16_out0[5], decoder_16_out0[6]);
  or X_X3X_4 (X_X2X_2_out[1], X_X3X_3_out, X_X3X_5_out);
  or X_X3X_5 (X_X3X_5_out, decoder_16_out0[7], decoder_16_out0[8], decoder_16_out0[9], decoder_16_out0[10], decoder_16_out0[11]);
  or X_X4X_2 (X_X4X_2_out, decoder_16_out0[12], decoder_16_out0[13], decoder_16_out0[14], decoder_16_out0[15], decoder_17_out0[0]);
  or X_X4X_3 (X_X2X_2_out[2], X_X4X_2_out, X_X4X_4_out);
  or X_X4X_4 (X_X4X_4_out, decoder_17_out0[1], decoder_17_out0[2], decoder_17_out0[3], decoder_17_out0[4], decoder_17_out0[5]);
  or X_X5X_2 (X_X5X_2_out, decoder_17_out0[6], decoder_17_out0[7], decoder_17_out0[8], decoder_17_out0[9], decoder_17_out0[10]);
  or X_X5X_3 (X_X2X_2_out[3], X_X5X_2_out, X_X5X_4_out);
  or X_X5X_4 (X_X5X_4_out, decoder_17_out0[11], decoder_17_out0[12], decoder_17_out0[13], decoder_17_out0[14], decoder_17_out0[15]);
  or X_1XX (X_1XX_out, X_X2X_2_out[3], X_X2X_2_out[2], X_X2X_2_out[1], X_X2X_2_out[0]);
  or X_X6X_2 (X_X6X_2_out, decoder_12_out0[0], decoder_12_out0[1], decoder_12_out0[2], decoder_12_out0[3], decoder_12_out0[4], decoder_12_out0[5]);
  or X_X9X (X_X9X_out, decoder_13_out0[10], decoder_13_out0[11], decoder_13_out0[12]);
  or X_X9X_2 (X_X9X_2_out, decoder_13_out0[13], decoder_13_out0[14], decoder_13_out0[15]);
  or X_X9X_3 (X_X9X_3_out, decoder_14_out0[0], decoder_14_out0[1], decoder_14_out0[2], decoder_14_out0[3]);
  or X_X0X_2 (X_X0X_2_out, decoder_14_out0[4], decoder_14_out0[5], decoder_14_out0[6], decoder_14_out0[7], decoder_14_out0[8]);
  or X_X0X_3 (X_X0X_3_out[0], X_X0X_2_out, X_X0X_4_out);
  or X_X0X_4 (X_X0X_4_out, decoder_14_out0[9], decoder_14_out0[10], decoder_14_out0[11], decoder_14_out0[12], decoder_14_out0[13]);
  or X_X1X_2 (X_X1X_2_out, decoder_14_out0[14], decoder_14_out0[15], decoder_15_out0[0], decoder_15_out0[1], decoder_15_out0[2]);
  or X_X1X_3 (X_X0X_3_out[1], X_X1X_2_out, X_X1X_4_out);
  or X_X1X_4 (X_X1X_4_out, decoder_15_out0[3], decoder_15_out0[4], decoder_15_out0[5], decoder_15_out0[6], decoder_15_out0[7]);
  or X_X2X_3 (X_X2X_3_out, decoder_15_out0[8], decoder_15_out0[9], decoder_15_out0[10], decoder_15_out0[11], decoder_15_out0[12]);
  or X_X2X_4 (X_X2X_4_out, X_X2X_3_out, X_X2X_5_out);
  or X_X2X_5 (X_X2X_5_out, decoder_15_out0[13], decoder_15_out0[14], decoder_15_out0[15]);
  or X_X7X (X_X4X_out[3], decoder_12_out0[6], decoder_12_out0[7], decoder_12_out0[8], decoder_12_out0[9], decoder_12_out0[10], decoder_12_out0[11], decoder_12_out0[12], decoder_12_out0[13], decoder_12_out0[14], decoder_12_out0[15]);
  or X_X8X (X_X4X_out[4], decoder_13_out0[0], decoder_13_out0[1], decoder_13_out0[2], decoder_13_out0[3], decoder_13_out0[4], decoder_13_out0[5], decoder_13_out0[6], decoder_13_out0[7], decoder_13_out0[8], decoder_13_out0[9]);
  or X_X9X_4 (X_X4X_out[5], X_X9X_out, X_X9X_2_out, X_X9X_3_out);
  or X_1XX_2 (X_1XX_2_out, X_X0X_3_out[0], X_X0X_3_out[1], X_X2X_4_out);
  or X_1XX_3 (X_0XX_2_out[1], X_1XX_2_out, X_1XX_4_out);
  or X_1XX_4 (X_1XX_4_out, X_1XX_out, X_1XX_5_out);
  or X_0XX_4 (X_0XX_4_out, X_X4X_out[3], X_X4X_out[4], X_X4X_out[5]);
  assign Tens_3_out = {X_X2X_2_out[7:1], X_X0X_3_out} | {{6{X_X0X_7_out[9]}}, X_X0X_7_out[3:0]};  // OR_Gate Tens_3, 10 bits wide
  or X_X2X_6 (X_X0X_3_out[2], X_X2X_4_out, X_X2X_2_out[0]);
  or X_XX1_6 (X_XX0_6_out[1], decoder_18_out0[1], decoder_18_out0[11], decoder_18_out0[21], decoder_18_out0[31]);
  or X_XX0_6 (X_XX0_6_out[0], decoder_18_out0[0], decoder_18_out0[10], decoder_18_out0[20], decoder_18_out0[30]);
  or X_XX1_7 (X_XX0_7_out[1], decoder_20_out0[9], decoder_21_out0[3]);
  or X_XX0_7 (X_XX0_7_out[0], decoder_20_out0[8], decoder_21_out0[2]);
  or X_XX2_6 (X_XX0_6_out[2], decoder_18_out0[2], decoder_18_out0[12], decoder_18_out0[22]);
  or X_XX3_6 (X_XX0_6_out[3], decoder_18_out0[3], decoder_18_out0[13], decoder_18_out0[23]);
  or X_XX2_7 (X_XX0_7_out[2], decoder_20_out0[0], decoder_20_out0[10], decoder_21_out0[4]);
  or X_XX3_7 (X_XX0_7_out[3], decoder_20_out0[1], decoder_20_out0[11], decoder_21_out0[5]);
  or X_XX4_6 (decoder_22_out6[4], decoder_22_out0[0], decoder_22_out0[10]);
  or X_XX5_6 (X_XX0_6_out[5], decoder_18_out0[5], decoder_18_out0[15], decoder_18_out0[25]);
  or X_XX4_7 (X_XX0_6_out[4], decoder_18_out0[4], decoder_18_out0[14], decoder_18_out0[24]);
  or X_XX6_6 (X_XX0_6_out[6], decoder_18_out0[6], decoder_18_out0[16], decoder_18_out0[26]);
  or X_XX5_7 (X_XX0_7_out[5], decoder_20_out0[3], decoder_20_out0[13], decoder_21_out0[7]);
  or X_XX4_8 (X_XX0_7_out[4], decoder_20_out0[2], decoder_20_out0[12], decoder_21_out0[6]);
  or X_XX6_7 (X_XX0_7_out[6], decoder_20_out0[4], decoder_20_out0[14], decoder_21_out0[8]);
  or X_XX6_8 (decoder_22_out6[6], decoder_22_out0[2], decoder_22_out0[12]);
  or X_XX5_8 (decoder_22_out6[5], decoder_22_out0[1], decoder_22_out0[11]);
  or X_XX7_6 (X_XX0_6_out[7], decoder_18_out0[7], decoder_18_out0[17], decoder_18_out0[27]);
  or X_XX8_6 (X_XX0_6_out[8], decoder_18_out0[8], decoder_18_out0[18], decoder_18_out0[28]);
  or X_XX7_7 (X_XX0_7_out[7], decoder_20_out0[5], decoder_20_out0[15], decoder_21_out0[9]);
  or X_XX8_7 (X_XX0_7_out[8], decoder_20_out0[6], decoder_21_out0[0], decoder_21_out0[10]);
  or X_XX8_8 (decoder_22_out6[8], decoder_22_out0[4], decoder_22_out0[14]);
  or X_XX7_8 (decoder_22_out6[7], decoder_22_out0[3], decoder_22_out0[13]);
  or X_XX9_6 (X_XX0_6_out[9], decoder_18_out0[9], decoder_18_out0[19], decoder_18_out0[29]);
  or X_X6X_3 (X_X6X_3_out, decoder_18_out0[0], decoder_18_out0[1], decoder_18_out0[2], decoder_18_out0[3], decoder_18_out0[4]);
  or X_X6X_4 (X_X6X_4_out, decoder_18_out0[5], decoder_18_out0[6], decoder_18_out0[7], decoder_18_out0[8], decoder_18_out0[9]);
  or X_X7X_2 (X_X7X_2_out, decoder_18_out0[10], decoder_18_out0[11], decoder_18_out0[12], decoder_18_out0[13], decoder_18_out0[14]);
  or X_X7X_3 (X_X7X_3_out, decoder_18_out0[15], decoder_18_out0[16], decoder_18_out0[17], decoder_18_out0[18], decoder_18_out0[19]);
  or X_X8X_2 (X_X8X_2_out, decoder_18_out0[20], decoder_18_out0[21], decoder_18_out0[22], decoder_18_out0[23], decoder_18_out0[24]);
  or X_X8X_3 (X_X8X_3_out, decoder_18_out0[25], decoder_18_out0[26], decoder_18_out0[27], decoder_18_out0[28], decoder_18_out0[29]);
  or X_XX9_7 (X_XX0_7_out[9], decoder_20_out0[7], decoder_21_out0[1], decoder_21_out0[11]);
  or X_X0X_5 (X_X0X_5_out, decoder_20_out0[8], decoder_20_out0[9], decoder_20_out0[10], decoder_20_out0[11], decoder_20_out0[12]);
  or X_X0X_6 (X_X0X_6_out, decoder_20_out0[13], decoder_20_out0[14], decoder_20_out0[15], decoder_21_out0[0], decoder_21_out0[1]);
  or X_X1X_5 (X_X1X_5_out, decoder_21_out0[2], decoder_21_out0[3], decoder_21_out0[4], decoder_21_out0[5], decoder_21_out0[6]);
  or X_X1X_6 (X_X1X_6_out, decoder_21_out0[7], decoder_21_out0[8], decoder_21_out0[9], decoder_21_out0[10], decoder_21_out0[11]);
  or X_X2X_7 (X_X0X_7_out[2], decoder_21_out0[12], decoder_21_out0[13], decoder_21_out0[14], decoder_21_out0[15], X_X2X_8_out);
  or X_XX9_8 (decoder_22_out6[9], decoder_22_out0[5], decoder_22_out0[15]);
  or X_X2X_8 (X_X2X_8_out, decoder_22_out0[0], decoder_22_out0[1], decoder_22_out0[2], decoder_22_out0[3], decoder_22_out0[4], decoder_22_out0[5]);
  or X_X3X_6 (X_X3X_6_out, decoder_22_out6[0], decoder_22_out6[1], decoder_22_out6[2], decoder_22_out6[3], decoder_22_out0[10]);
  or X_X3X_7 (X_X3X_7_out, decoder_22_out0[11], decoder_22_out0[12], decoder_22_out0[13], decoder_22_out0[14], decoder_22_out0[15]);
  or X_X6X_5 (X_X2X_2_out[4], X_X6X_3_out, X_X6X_4_out);
  or X_X7X_4 (X_X2X_2_out[5], X_X7X_2_out, X_X7X_3_out);
  or X_X8X_4 (X_X2X_2_out[6], X_X8X_2_out, X_X8X_3_out);
  or X_X9X_5 (X_X2X_2_out[7], decoder_18_out0[30], decoder_18_out0[31], X_X9X_6_out);
  or X_X9X_6 (X_X9X_6_out, decoder_20_out0[0], decoder_20_out0[1], decoder_20_out0[2], decoder_20_out0[3], decoder_20_out0[4], decoder_20_out0[5], decoder_20_out0[6], decoder_20_out0[7]);
  or X_X0X_7 (X_X0X_7_out[0], X_X0X_5_out, X_X0X_6_out);
  or X_X1X_7 (X_X0X_7_out[1], X_X1X_5_out, X_X1X_6_out);
  or X_X3X_8 (X_X0X_7_out[3], X_X3X_6_out, X_X3X_7_out);
  or X_1XX_5 (X_1XX_5_out, X_X2X_2_out[4], X_X2X_2_out[5], X_X2X_2_out[6], X_X2X_2_out[7]);
  or X_2XX (X_0XX_2_out[2], X_X0X_7_out[0], X_X0X_7_out[1], X_X0X_7_out[2], X_X0X_7_out[3]);

  // Notes on the sheet:
  //   Started: 2:31 PM 2/27/20
  //   Ended: 12:24 AM 3/1/20
  //   Created by: Nicholas Melito
  //   E = Divide By 0 Error
endmodule
